// Logisim project Guess_The_Number_Xtreme.circ as structural Verilog
module Flip_Flop_SR (
  input  S_R,
  input  Clock,
  input  Preset,
  input  Enable,
  input  Clear,
  output out_6
);

  wire not_1_out;

  not not_1 (not_1_out, S_R);
  S_R_Flip_Flop s_r_ff_1 (
    .S(S_R), .clk(Clock), .R(not_1_out), .Q(out_6), .preset(Preset), .reset(Clear), .en(Enable));  // open: Qn
endmodule

module Decrementador (
  input  Clock,
  input  Preset,
  input  Enable,
  input  Clear,
  input  [3:0] valor_retorno,
  output [3:0] out_6
);

  wire comparator_1_eq;
  wire [3:0] adder_1_out, multiplexer_1_out;

  Hex_Digit_Display hex_digit_display_1 (.value(out_6));  // open: dp
  Flip_Flop_SR flip_flop_sr_1 (
    .S_R(multiplexer_1_out[3]), .Clock(Clock), .Preset(Preset), .Enable(Enable), .Clear(Clear),
    .out_6(out_6[3]));
  Flip_Flop_SR flip_flop_sr_2 (
    .S_R(multiplexer_1_out[2]), .Clock(Clock), .Preset(Preset), .Enable(Enable), .Clear(Clear),
    .out_6(out_6[2]));
  Flip_Flop_SR flip_flop_sr_3 (
    .S_R(multiplexer_1_out[1]), .Clock(Clock), .Preset(Preset), .Enable(Enable), .Clear(Clear),
    .out_6(out_6[1]));
  Multiplexer #(.width(4)) multiplexer_1 (
    .in0(adder_1_out), .in1(valor_retorno), .out(multiplexer_1_out), .sel(comparator_1_eq));  // open: en
  Flip_Flop_SR flip_flop_sr_4 (
    .S_R(multiplexer_1_out[0]), .Clock(Clock), .Preset(Preset), .Enable(Enable), .Clear(Clear),
    .out_6(out_6[0]));
  Hex_Digit_Display hex_digit_display_2 (.value(adder_1_out));  // open: dp
  Adder #(.width(4)) adder_1 (.a(out_6), .b(4'b1111), .out(adder_1_out));  // open: cin, cout
  Comparator #(.width(4)) comparator_1 (.a(adder_1_out), .b(4'b1111), .eq(comparator_1_eq));  // open: gt, lt
endmodule

module Verificador_9 (
  input  Enable
);

  wire and_1_out, clock_1_out, comparator_1_eq, comparator_2_eq, comparator_3_eq, comparator_4_eq, not_1_out;
  wire [3:0] and_2_out, decrementador_1_out_6, decrementador_2_out_6, decrementador_3_out_6,
       decrementador_4_out_6;

  and and_1 (and_1_out, Enable, not_1_out);
  not not_1 (not_1_out, comparator_2_eq);
  Hex_Digit_Display hex_digit_display_1 (.value(decrementador_1_out_6));  // open: dp
  Decrementador decrementador_1 (
    .Clock(comparator_1_eq), .Enable(and_1_out), .valor_retorno(4'b0101), .out_6(decrementador_1_out_6));  // open: Preset, Clear
  Hex_Digit_Display hex_digit_display_2 (.value(decrementador_2_out_6));  // open: dp
  Decrementador decrementador_2 (
    .Clock(comparator_3_eq), .Enable(and_1_out), .valor_retorno(4'b1001), .out_6(decrementador_2_out_6));  // open: Preset, Clear
  Comparator #(.width(4)) comparator_1 (.a(decrementador_2_out_6), .b(4'b1001), .eq(comparator_1_eq));  // open: gt, lt
  assign and_2_out = ~decrementador_1_out_6 & ~decrementador_2_out_6 & ~decrementador_3_out_6 & ~decrementador_4_out_6;  // AND_Gate and_2, 4 bits wide
  Hex_Digit_Display hex_digit_display_3 (.value(decrementador_3_out_6));  // open: dp
  Decrementador decrementador_3 (
    .Clock(comparator_4_eq), .Enable(and_1_out), .valor_retorno(4'b0101), .out_6(decrementador_3_out_6));  // open: Preset, Clear
  Comparator #(.width(4)) comparator_2 (.a(and_2_out), .b(4'b1111), .eq(comparator_2_eq));  // open: gt, lt
  Comparator #(.width(4)) comparator_3 (.a(decrementador_3_out_6), .b(4'b0101), .eq(comparator_3_eq));  // open: gt, lt
  Hex_Digit_Display hex_digit_display_4 (.value(decrementador_4_out_6));  // open: dp
  Decrementador decrementador_4 (
    .Clock(clock_1_out), .Enable(and_1_out), .valor_retorno(4'b1001), .out_6(decrementador_4_out_6));  // open: Preset, Clear
  Comparator #(.width(4)) comparator_4 (.a(decrementador_4_out_6), .b(4'b1001), .eq(comparator_4_eq));  // open: gt, lt
  Clock clock_1 (.out(clock_1_out));
endmodule

module decrementar_min_sec (
  input  Enable,
  input  Clear,
  input  Clock,
  input  Clear_2,
  input  Enable_2
);

  wire and_2_out, button_1_out, button_2_out, button_3_out, button_4_out, clock_1_out, comparator_1_eq,
       comparator_2_eq, comparator_3_eq, comparator_4_eq, multiplexer_1_out, multiplexer_2_out,
       multiplexer_3_out, multiplexer_4_out, not_1_out, not_2_out, or_1_out, or_2_out, or_3_out, or_4_out;
  wire [3:0] and_1_out, decrementador_1_out_6, decrementador_2_out_6, decrementador_3_out_6,
       decrementador_4_out_6;

  not not_1 (not_1_out, Enable_2);
  Hex_Digit_Display hex_digit_display_1 (.value(decrementador_1_out_6));  // open: dp
  Decrementador decrementador_1 (
    .Clock(multiplexer_1_out), .Enable(or_1_out), .valor_retorno(4'b0101), .out_6(decrementador_1_out_6));  // open: Preset, Clear
  or or_1 (or_1_out, Enable_2, not_1_out);
  Multiplexer multiplexer_1 (
    .in0(button_1_out), .in1(comparator_1_eq), .out(multiplexer_1_out), .sel(Enable_2));  // open: en
  Button button_1 (.out(button_1_out));
  Hex_Digit_Display hex_digit_display_2 (.value(decrementador_2_out_6));  // open: dp
  Decrementador decrementador_2 (
    .Clock(multiplexer_2_out), .Enable(or_2_out), .valor_retorno(4'b1001), .out_6(decrementador_2_out_6));  // open: Preset, Clear
  or or_2 (or_2_out, Enable_2, not_1_out);
  Multiplexer multiplexer_2 (
    .in0(button_2_out), .in1(comparator_2_eq), .out(multiplexer_2_out), .sel(Enable_2));  // open: en
  Button button_2 (.out(button_2_out));
  Comparator #(.width(4)) comparator_1 (.a(decrementador_2_out_6), .b(4'b1001), .eq(comparator_1_eq));  // open: gt, lt
  assign and_1_out = ~decrementador_1_out_6 & ~decrementador_2_out_6 & ~decrementador_3_out_6 & ~decrementador_4_out_6;  // AND_Gate and_1, 4 bits wide
  Hex_Digit_Display hex_digit_display_3 (.value(decrementador_3_out_6));  // open: dp
  Decrementador decrementador_3 (
    .Clock(multiplexer_3_out), .Enable(or_3_out), .valor_retorno(4'b0101), .out_6(decrementador_3_out_6));  // open: Preset, Clear
  or or_3 (or_3_out, Enable_2, not_1_out);
  Multiplexer multiplexer_3 (
    .in0(button_3_out), .in1(comparator_4_eq), .out(multiplexer_3_out), .sel(Enable_2));  // open: en
  Button button_3 (.out(button_3_out));
  Comparator #(.width(4)) comparator_2 (.a(decrementador_3_out_6), .b(4'b0101), .eq(comparator_2_eq));  // open: gt, lt
  Comparator #(.width(4)) comparator_3 (.a(and_1_out), .b(4'b1111), .eq(comparator_3_eq));  // open: gt, lt
  Hex_Digit_Display hex_digit_display_4 (.value(decrementador_4_out_6));  // open: dp
  Decrementador decrementador_4 (
    .Clock(multiplexer_4_out), .Enable(or_4_out), .valor_retorno(4'b1001), .out_6(decrementador_4_out_6));  // open: Preset, Clear
  or or_4 (or_4_out, Enable_2, not_1_out);
  Multiplexer multiplexer_4 (.in0(button_4_out), .in1(and_2_out), .out(multiplexer_4_out), .sel(Enable_2));  // open: en
  Button button_4 (.out(button_4_out));
  Comparator #(.width(4)) comparator_4 (.a(decrementador_4_out_6), .b(4'b1001), .eq(comparator_4_eq));  // open: gt, lt
  and and_2 (and_2_out, not_2_out, clock_1_out);
  Clock clock_1 (.out(clock_1_out));
  not not_2 (not_2_out, comparator_3_eq);
endmodule

module Entrada (
  input  A3,
  input  A2,
  input  A1,
  input  A0
);

  Hex_Digit_Display hex_digit_display_1 (.value({A3, A2, A1, A0}));  // open: dp
endmodule

module Coordenadas (
  input  [3:0] in_1,
  input  [3:0] in_2,
  input  [3:0] in_3,
  input  \Próximo ,
  input  \Próximo_2 ,
  output [3:0] out_6
);

  wire and_1_out, and_2_out, button_1_out, chutar_out, comparator_1_eq, comparator_2_eq, comparator_3_eq,
       proximo_out;
  wire [3:0] flip_flop_condicao_1_valor_saida, multiplexer_1_out, multiplexer_4_out, register_1_q,
       register_2_q, undriven, undriven_2;

  Button button_1 (.out(button_1_out));
  D_Flip_Flop d_ff_1 (.clk(button_1_out));  // open: D, Q, Qn, preset, en, reset
  Hex_Digit_Display hex_digit_display_1 (.value(in_2));  // open: dp
  Multiplexer #(.width(4)) multiplexer_1 (
    .in0(in_2), .in1(in_3), .out(multiplexer_1_out), .en(\Próximo ));  // open: sel
  Multiplexer #(.width(4), .disabled(0)) multiplexer_2 (
    .in0(undriven), .in1(undriven_2), .out(multiplexer_1_out), .sel(\Próximo_2 ));  // open: en
  Hex_Digit_Display hex_digit_display_2 (.value(undriven));  // open: dp
  Hex_Digit_Display hex_digit_display_3 (.value(undriven_2));  // open: dp
  Hex_Digit_Display hex_digit_display_4 (.value(in_3));  // open: dp
  D_Flip_Flop d_ff_2 ();  // open: clk, D, Q, Qn, preset, en, reset
  Button proximo (.out(proximo_out));
  flip_flop_condicao flip_flop_condicao_1 (
    .Clock(proximo_out), .Preset(1'b0), .Enable(1'b1), .Clear(1'b0), .valor_retorno(4'b0000),
    .valor_max__1(4'b0010), .valor_saida(flip_flop_condicao_1_valor_saida));
  Button chutar (.out(chutar_out));
  Comparator #(.width(4)) comparator_1 (
    .a(flip_flop_condicao_1_valor_saida), .b(4'b0001), .eq(comparator_1_eq));  // open: gt, lt
  and and_1 (and_1_out, chutar_out, ~comparator_1_eq);  // AND_Gate
  Multiplexer #(.width(4)) multiplexer_3 (.in0(in_1), .out(out_6), .sel(and_1_out));  // open: in1, en
  Hex_Digit_Display hex_digit_display_5 (.value(register_1_q));  // open: dp
  Comparator #(.width(4)) comparator_2 (
    .a(flip_flop_condicao_1_valor_saida), .b(4'b0000), .eq(comparator_2_eq));  // open: gt, lt
  LED led_1 (.in(comparator_2_eq));
  and and_2 (and_2_out, chutar_out, comparator_1_eq);
  Register #(.width(4)) register_1 (.D(out_6), .Q(register_1_q), .clk(and_1_out));  // open: en, clr
  Multiplexer #(.width(4)) multiplexer_4 (
    .in0(in_1), .in1(in_1), .out(multiplexer_4_out), .sel(and_2_out));  // open: en
  Register #(.width(4)) register_2 (.D(multiplexer_4_out), .Q(register_2_q), .clk(and_2_out));  // open: en, clr
  Hex_Digit_Display hex_digit_display_6 (.value(register_2_q));  // open: dp
  Comparator #(.width(4)) comparator_3 (
    .a(flip_flop_condicao_1_valor_saida), .b(4'b0001), .eq(comparator_3_eq));  // open: gt, lt
  LED led_2 (.in(comparator_3_eq));
  Hex_Digit_Display hex_digit_display_7 ();  // open: value, dp
endmodule

module flip_flop_condicao (
  input  Clock,
  input  Preset,
  input  Enable,
  input  Clear,
  input  [3:0] valor_retorno,
  input  [3:0] valor_max__1,
  output [3:0] valor_saida
);

  wire comparator_1_eq;
  wire [3:0] adder_1_out, multiplexer_1_out;

  Hex_Digit_Display hex_digit_display_1 (.value(valor_saida));  // open: dp
  Flip_Flop_SR flip_flop_sr_1 (
    .S_R(multiplexer_1_out[3]), .Clock(Clock), .Preset(Preset), .Enable(Enable), .Clear(Clear),
    .out_6(valor_saida[3]));
  Flip_Flop_SR flip_flop_sr_2 (
    .S_R(multiplexer_1_out[2]), .Clock(Clock), .Preset(Preset), .Enable(Enable), .Clear(Clear),
    .out_6(valor_saida[2]));
  Flip_Flop_SR flip_flop_sr_3 (
    .S_R(multiplexer_1_out[1]), .Clock(Clock), .Preset(Preset), .Enable(Enable), .Clear(Clear),
    .out_6(valor_saida[1]));
  Multiplexer #(.width(4)) multiplexer_1 (
    .in0(adder_1_out), .in1(valor_retorno), .out(multiplexer_1_out), .sel(comparator_1_eq));  // open: en
  Flip_Flop_SR flip_flop_sr_4 (
    .S_R(multiplexer_1_out[0]), .Clock(Clock), .Preset(Preset), .Enable(Enable), .Clear(Clear),
    .out_6(valor_saida[0]));
  Hex_Digit_Display hex_digit_display_2 (.value(adder_1_out));  // open: dp
  Adder #(.width(4)) adder_1 (.a(valor_saida), .b(4'b0001), .out(adder_1_out));  // open: cin, cout
  Comparator #(.width(4)) comparator_1 (.a(adder_1_out), .b(valor_max__1), .eq(comparator_1_eq));  // open: gt, lt
endmodule
